// Logisim project cpu.circ as structural Verilog: 1 circuit, main circuit cpu
module cpu (
  output [31:0] out_1,
  output [31:0] out_2,
  output out_3,
  output out_4,
  output out_5,
  output [5:0] out_6,
  output out_7,
  output out_8
);

  wire ALU_Src, and_1_out, and_2_out, and_3_out, cache_1_p22, Finish, mem_fetch_done, mem_mask_sel,
       not_1_out, not_2_out, not_3_out, not_4_out, not_5_out, not_6_out, not_7_out, Reg_Write,
       RegisterFile_p7, Zero;
  wire [1:0] mem_data_sel, MEMW_Sel, PC_control, Reg_Dest, Reg_Write_Sel, Shift_Select;
  wire [2:0] mem_addr_sel;
  wire [3:0] decoder_1_out0, multiplexer_7_out, multiplexer_10_out;
  wire [4:0] ALU_Ctrl, multiplexer_3_out, multiplexer_6_out;
  wire [5:0] Func;
  wire [7:0] miss_counter_state;
  wire [25:6] J_addr;
  wire [27:0] PC;
  wire [31:0] ALU_Result, cache_1_p10, cache_1_p11, cache_1_p12, cache_1_p13, cache_1_p14, cache_1_p15,
       cache_1_p16, cache_1_p17, cache_1_p18, cache_1_p19, cache_1_p20, cache_1_p21, Imm_ext, J_value,
       multiplexer_1_out, multiplexer_4_out, multiplexer_5_out, multiplexer_9_out, multiplexer_11_out, newPC,
       PC_4, PC_4_Imm, Read_Data1, Read_Data2, shifter_1_out;

  Shifter #(.width(32)) shifter_1 (.in(Imm_ext), .\dist (5'b00010), .out(shifter_1_out));
  PLA #(.in_width(6), .out_width(1), .\table ("100011 1 # LW\n100000 1 # LB\n101000 1 # SB\n101011 1 # SW")) Checker (
    .in(out_6), .out(out_3));
  not not_1 (not_1_out, Finish);
  not not_2 (not_2_out, out_5);
  Adder #(.width(32)) adder_1 (.a({J_value[31:28], PC}), .b(32'h4), .out(PC_4));  // open: cin, cout
  Adder #(.width(32)) adder_2 (.a(PC_4), .b(shifter_1_out), .out(PC_4_Imm));  // open: cin, cout
  Shifter #(.width(28)) shifter_2 (.in({2'b00, J_addr, Func}), .\dist (5'b00010), .out(J_value[27:0]));
  Register #(.width(32)) u_PC (.D(newPC), .en(not_1_out), .clk(not_2_out), .Q({J_value[31:28], PC}));  // open: clr
  not not_3 (not_3_out, out_5);
  Multiplexer #(.width(32)) multiplexer_1 (.in0(PC_4_Imm), .in1(PC_4), .out(multiplexer_1_out), .sel(Zero));
  Multiplexer #(.select(2), .width(32)) multiplexer_2 (
    .in0(PC_4), .in1(multiplexer_1_out), .in2(J_value), .in3(Read_Data1), .out(newPC), .sel(PC_control));
  mem InstMem (
    .MemAddress({J_value[31:28], PC}), .MemWriteMask(4'b0000), .MemWriteData({32{1'b1}}), .clk(not_3_out),
    .MemReadData({out_6, J_addr, Func}));
  assign Imm_ext = {{16{J_addr[15]}}, {J_addr[15:6], Func}};  // Bit_Extender bit_extender_1
  // control_unit CU: pin names not known; wires that end beside it: out_6, Func, Reg_Write, ALU_Src, PC_control, Reg_Dest, Reg_Write_Sel, MEMW_Sel, Finish
  Multiplexer #(.select(2), .width(5)) multiplexer_3 (
    .in0(J_addr[20:16]), .in1(J_addr[15:11]), .in2({5{1'b1}}), .in3(5'b00001), .out(multiplexer_3_out),
    .sel(Reg_Dest));
  Multiplexer #(.select(2), .width(32)) multiplexer_4 (
    .in0(ALU_Result), .in1(out_2), .in2({J_value[31:28], PC}), .in3({{24{1'b0}}, out_2[7:0]}),
    .out(multiplexer_4_out), .sel(Reg_Write_Sel));
  Multiplexer #(.width(32)) multiplexer_5 (.in0(Read_Data2), .in1(Imm_ext), .out(multiplexer_5_out), .sel(ALU_Src));
  Decoder #(.enable("false"), .select(2)) decoder_1 (
    .out0(decoder_1_out0[0]), .out1(decoder_1_out0[1]), .out2(decoder_1_out0[2]), .out3(decoder_1_out0[3]),
    .sel(ALU_Result[1:0]));
  Clock clock_1 (.out(out_4));
  Multiplexer #(.select(2), .width(5)) multiplexer_6 (
    .in0(J_addr[10:6]), .in1(Read_Data1[4:0]), .in2(5'b10000), .in3({5{1'b0}}), .out(multiplexer_6_out),
    .sel(Shift_Select));
  // regfile RegisterFile: pin names not known; wires that end beside it: J_addr[25:21], J_addr[20:16], multiplexer_3_out, multiplexer_4_out, Reg_Write, out_5, RegisterFile_p7, Read_Data1, Read_Data2
  not not_4 (not_4_out, out_4);
  and and_1 (and_1_out, out_4, out_7);
  Multiplexer #(.select(2), .width(4)) multiplexer_7 (
    .in0(4'b0000), .in1(4'b1111), .in2(decoder_1_out0), .in3(4'b0000), .out(multiplexer_7_out), .sel(MEMW_Sel));
  not not_5 (not_5_out, out_4);
  and and_2 (and_2_out, not_4_out, out_3);
  Multiplexer multiplexer_8 (.in0(out_4), .in1(and_1_out), .out(out_5), .sel(out_3));
  Counter #(.max('h12)) counter_1 (
    .clr(out_7), .load(1'b0), .up(1'b1), .clk(and_2_out), .Q(miss_counter_state));  // open: count, D, carry
  ALU ArithLogicUnit (
    .Input1(Read_Data1), .Input2(multiplexer_5_out), .op(ALU_Ctrl), .SHA(multiplexer_6_out), .Zero(Zero),
    .Result(ALU_Result));
  // Cache cache_1: pin names not known; wires that end beside it: Read_Data2, ALU_Result, not_5_out, multiplexer_7_out, miss_counter_state, out_1, out_3, out_7, out_2, cache_1_p10, cache_1_p11, cache_1_p12, cache_1_p13, cache_1_p14, cache_1_p15, cache_1_p16, cache_1_p17, cache_1_p18, cache_1_p19, cache_1_p20, cache_1_p21, cache_1_p22
  and and_3 (and_3_out, cache_1_p22, mem_mask_sel);
  not not_6 (not_6_out, out_4);
  not not_7 (not_7_out, out_7);
  alu_control_unit ALU_Control (.func(Func), .opcode(out_6), .ALU_control_bits(ALU_Ctrl), .Shift_Select(Shift_Select));
  Multiplexer #(.select(3), .width(32)) multiplexer_9 (
    .in0(cache_1_p10), .in1(cache_1_p11), .in2(cache_1_p12), .in3(cache_1_p13), .in4(cache_1_p14),
    .in5(cache_1_p15), .in6(cache_1_p16), .in7(cache_1_p17), .out(multiplexer_9_out), .sel(mem_addr_sel));
  Multiplexer #(.width(4)) multiplexer_10 (.in0(4'b0000), .in1(4'b1111), .out(multiplexer_10_out), .sel(and_3_out));
  Multiplexer #(.select(2), .width(32)) multiplexer_11 (
    .in0(cache_1_p18), .in1(cache_1_p19), .in2(cache_1_p20), .in3(cache_1_p21), .out(multiplexer_11_out),
    .sel(mem_data_sel));
  and and_4 (out_8, not_6_out, out_3, not_7_out);
  PLA #(.in_width(8), .out_width(7), .\table ("00000000 0001000 # w0_wb_addr\n00000001 0011001 # w1_wb_addr\n00000010 0101010 # w2 wb_addr\n00000011 0111011 # w3_wb_addr\n00000100 0000100 # w0_fetch_addr\n00000101 0000101 # w1_fetch_addr\n00000110 0000110 # w2_fetch_addr\n00000111 0000111 # w3_fetch_addr\n00010001 1000000 # mem_done")) miss_controls (
    .in(miss_counter_state), .out({mem_fetch_done, mem_data_sel, mem_mask_sel, mem_addr_sel}));
  memDelayed memdelayed_1 (
    .MemAddress(multiplexer_9_out), .MemWriteMask(multiplexer_10_out), .MemWriteData(multiplexer_11_out),
    .clk(out_8), .MemReadData(out_1));

  // Other names for the same wires on the sheet: J_addr[5:0] = Func; SHA[4:0] = J_addr[10:6]; rd[4:0] = J_addr[15:11];
  //   rt[4:0] = J_addr[20:16]; rs[4:0] = J_addr[25:21]; opcode[5:0] = out_6; MemReadData[31:0] = out_2; hit = out_7;
  //   is_mem_inst = out_3; PC[31:28] = J_value[31:28]; Main_Clock = out_4; main_mem_read_data[31:0] = out_1;
  //   reading_from_mem = out_8; Secondary_Clock = out_5

  // Notes on the sheet:
  //   PC Logic
  //   Clk_Check
  //   Test_Outs
  //   Next
  //   Branch
  //   Jump
  //   JR
  //   Clock
  //   Cache-memory
  //   is_bit_valid
endmodule
